# Fritzing sketch midisister (saved by Fritzing 0.9.8b)
circuit board: 2.03607cm x 5.16028cm

parts:
  TRS2 = Audio Jack (TRS) 3.5mm [package="4Ucon 08780 [THT]"]
  R3 = Resistor [tolerance=±5% power=0.25 resistance=33 package=THT]
  ohno = LED - 3mm [color="Orange (620nm)" current=0.030 package="3 mm [THT]"]
  R5 = Resistor [tolerance=±5% power=0.25 resistance=100 package=THT]
  nun = male pin header, 4 pins [form="♂ (male)"]
  Mod2 = Raspberry Pi Pico SISTER
  R4 = Resistor [tolerance=±5% power=0.25 resistance=10 package=THT]

nets:
  N1: TRS2.Ring, R3.Pin_1
  N2: TRS2.Tip, R4.Pin_0
  N3: R3.Pin_0, nun.pin3, Mod2.pin_36
  GND: ohno.cathode, nun.pin4, Mod2.pin_3, Mod2.pin_13, Mod2.pin_33
  N4: ohno.anode, R5.Pin_1
  N5: R5.Pin_0, Mod2.pin_24
  N6: nun.pin1, Mod2.pin_32
  N7: nun.pin2, Mod2.pin_31
  N8: Mod2.pin_21, R4.Pin_1

notes:
  GND
  midisister
  molentech
  rev1
  it's habit
  forming

custom parts:
  Raspberry Pi Pico SISTER: Raspberry Pi Pico. Based around the RP2040 microcontroller the Pico is a low cost microcontroller device bringing Raspberry Pi quality, cost, and easy of use to the microcontroller space. Jan 2021, Split part in to two versions: tht (this one) and SMD. This one will drill holes for a .1 in header in pcb to allow plugging in the module as well as providing pads to solder the module to the top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
